# Fritzing sketch linefollower-circuit (saved by Fritzing 1.0.4)

parts:
  Part1 = ESP12E Motor Shield
  Part2 = Pololu 3.3V Step-Up Voltage Regulator U1V11F3
  Part3 = Pololu 3.3V Step-Up Voltage Regulator U1V11F3
  VCC1 = Battery
  M1 = 5-ir-array-sensor [package=THT]
  Mod1 = Amica NodeMCU DEVKIT 1.0

nets:
  N1: Part1.D0#0, M1.S1
  N2: Part1.D1, Part1.G#6, Part1.D8#10, M1.S2, M1.GND
  N3: Part1.D2, M1.S3
  N4: Part1.D3, M1.S4
  N5: Part1.D4, M1.S5
  N6: Part1.3V3#5, M1.VCC
  N7: Part1.RST#17, Part1.3V3#19, Part1.3V3#47, Part1.3V3#54, Mod1.pin1, Mod1.pin_10, Mod1.pin_26
  N8: Part1.G#33, Part1.G#44, Part1.G#48, Part1.G#55, Mod1.pin2, Mod1.pin_9, Mod1.pin_25, Mod1.pin_29
  N9: Part1.SD0, Mod1.pin_23
  N10: Part1.CMD, Mod1.pin_22
  N11: Part1.SD1, Mod1.pin_21
  N12: Part1.RSV#40, Mod1.pin_18
  N13: Part1.VIN#43, Mod1.pin_30
  N14: Part1.RST#45, Mod1.pin_28
  N15: Part1.EN, Mod1.pin_27
  N16: Part1.CLK, Mod1.pin_24
  N17: Part1.SD2, Mod1.pin_20
  N18: Part1.SD3, Mod1.pin_19
  N19: Part1.RSV#52, Mod1.pin_17
  N20: Part1.AD0, Mod1.pin_16
  N21: Part1.TX, Mod1.pin3
  N22: Part1.RX, Mod1.pin4
  N23: Part1.D8#58, Mod1.pin5
  N24: Part1.D7, Mod1.pin6
  N25: Part1.D6, Mod1.pin7
  N26: Part1.D5, Mod1.pin8
  N27: Part1.CB, Mod1.pin_11
  N28: Part1.DA, Mod1.pin_12
  N29: Part1.PWMB, Mod1.pin_13
  N30: Part1.PWMA, Mod1.pin_14
  N31: Part1.D0#66, Mod1.pin_15
  N32: Part1.A-, Part2.IN1
  N33: Part1.A+, Part2.IN2
  N34: Part1.B-, Part3.IN2
  N35: Part1.B+, Part3.IN1
  N36: Part1.VIN#102, VCC1.+
  N37: Part1.GND, VCC1.-

custom parts:
  ESP12E Motor Shield: ESP8266 WiFi Motor Drive Expansion Board For NodeMCU ESP-12E
  Battery: Your standard 2x 18650 battery pack (7,4 Volts)
  5-ir-array-sensor: 5 IR array sensor.
